# Fritzing sketch controller (saved by Fritzing 0.9.3b)
circuit board: 8.46667cm x 5.64444cm
breadboards: 2

parts:
  J1 = Basic Servo
  R1 = Trimmer Potentiometer [maximum_resistance=10kΩ package=THT]
  Part1 = Arduino Uno (Rev3)
  S1 = Momentary Switch [package=ksa_sealed_tac_switch]
  S2 = Momentary Switch [package=ksa_sealed_tac_switch]
  S3 = Momentary Switch [package=ksa_sealed_tac_switch]
  S4 = Momentary Switch [package=ksa_sealed_tac_switch]
  U1 = PCF8574 [package="DIP16 [THT]"]
  R2 = Resistor [tolerance=±5% resistance=220 package=THT]
  LED1 = LED - 5mm [color="Red (633nm)" package="5 mm [THT]"]
  LED2 = LED - 5mm [color="Red (633nm)" package="5 mm [THT]"]
  LED3 = LED - 5mm [color="Red (633nm)" package="5 mm [THT]"]
  LED4 = LED - 5mm [color="Red (633nm)" package="5 mm [THT]"]
  Part2 = HX711 Weighing Sensor Module
  U2 = mystery part, 3 pins [chip_label="TLE4905L Hallotron"]
  C1 = Capacitor [part_number=4.7nF package=cap-pth-5mm]
  R3 = Resistor [tolerance=±5% resistance=1.2k package=THT]
  C2 = Capacitor [part_number=4.7nF package=cap-pth-5mm]
  GLCD_128x1 = LCD screen

nets (from the breadboard view):
  GND: J1.gnd, R1.leg2, U1.A0, U1.A1, U1.A3, U1.GND, LED1.cathode, LED2.cathode, LED3.cathode, LED4.cathode, Part2.GND, U2.pin2, C1.1, C2.2
  N1: J1.pulse, Part1.D9_PWM
  VCC: R1.leg1, Part1.5V, S1.1, S2.1, S3.1, S4.1, U1.VCC, Part2.VCC, U2.pin1, R3.Pin_0, C2.1
  N2: R1.wiper, GLCD_128x1.V0
  N3: Part1.A0, Part2.DO/RX
  N4: Part1.A1, Part2.CK/TX
  N5: Part1.A4/SDA, U1.SDA
  N6: Part1.A5/SCL, U1.SCL
  N7: Part1.D8, S3.4
  N8: Part1.D10_PWM/SS, S2.4
  N9: Part1.D2, U2.pin3, C1.2, R3.Pin_1
  N10: Part1.D6_PWM, S1.4
  N11: Part1.D7, S4.4
  N12: S1.3, LED1.anode
  N13: S2.3, LED4.anode
  N14: S3.3, LED3.anode
  N15: S4.3, LED2.anode
  N16: U1.P0, GLCD_128x1.DB4
  N17: U1.P1, GLCD_128x1.DB5
  N18: U1.P2, GLCD_128x1.DB6
  N19: U1.P3, GLCD_128x1.DB7
  N20: U1.P4, GLCD_128x1.E
  N21: U1.P5, GLCD_128x1.R/W
  N22: U1.P6, GLCD_128x1.RS
  N23: R2.Pin_0, GLCD_128x1.LED+
  VSS: GLCD_128x1.VSS, GLCD_128x1.VDD, GLCD_128x1.LED-
