# Fritzing sketch digispark (saved by Fritzing 0.9.3b)
circuit board: 8.46667cm x 5.64444cm

parts:
  Digispark1 = Digispark
  GY1 = MPU-6050 Board GY-521 [form="♀ (female)" package=THT]
  VCC1 = Battery
  S1 = Square Pushbutton
  U1 = Mystery Part - 2 pins [chip_label=? package=THT]
  J1 = Basic Servo

nets:
  N1: Digispark1.VCC, GY1.pin1, S1.leg1
  GND: Digispark1.GND, GY1.pin2, U1.VOUT-, J1.gnd
  VIN: Digispark1.VIN, U1.VOUT+, J1.vcc
  N2: Digispark1.P0, GY1.pin4
  N3: Digispark1.P2, GY1.pin3
  N4: Digispark1.P4, J1.pulse
  N5: Digispark1.P5, S1.leg0
  N6: VCC1.-, U1.VIN-
  N7: VCC1.+, U1.VIN+

custom parts:
  Digispark: The Digispark is an Attiny85 based microcontroller development board similar to the Arduino line, only cheaper, smaller, and a bit less powerful. With a whole host of shields to extend its functionality and the ability to use the familiar Arduino IDE the Digispark is a great way to jump into electronics, or perfect for when an Arduino is too big or too much.
  MPU-6050 Board GY-521: Acelerometro y Giroscopio MPU-6050 Board GY-521
  Mystery Part - 2 pins: A dummy, proxy, ersatz, stand-in part for whatever you want. With 2 pins on a 100 mil inline pin header footprint.
